# Fritzing sketch Calc_Hub_Schematic_Diagram (saved by Fritzing 0.9.3b)
breadboards: 1

parts:
  Part1 = LCD1602-I2C
  Part2 = 4x4 Keypad [part_number=101207]
  Part3 = Arduino Uno (Rev3) - ICSP

nets:
  GND: Part1.GND, Part3.GND
  VCC: Part1.VCC, Part3.5V
  N1: Part1.SDA, Part3.A4/SDA
  N2: Part1.SCL, Part3.A5/SCL
  N3: Part2.1, Part3.D9_PWM
  N4: Part2.2, Part3.D8
  N5: Part2.3, Part3.D7
  N6: Part2.4, Part3.D6_PWM
  N7: Part2.5, Part3.D5_PWM
  N8: Part2.6, Part3.D4
  N9: Part2.7, Part3.D3_PWM
  N10: Part2.8, Part3.D2

notes:
  Keypad 4x4
  I2C 2X16 LCD
  Arduino Uno
  +
  -
  *
  /
  =
  C

custom parts:
  LCD1602-I2C: A standard character display, usually with 2x16 characters. Comes in many colors with LCM1602 IIC attached.
  4x4 Keypad: Matrix membrane keypad 4x4
